# Fritzing sketch 18naJednoArduino (saved by Fritzing 0.9.3b)
breadboards: 1

parts:
  Part1 = Arduino Uno (Rev3)
  LED1 = LED - 5mm [color="Red (633nm)" package="5 mm [THT]"]
  R1 = Resistor [tolerance=±5% resistance=220 package=THT]
  S1 = Pushbutton [package="[THT]"]
  S2 = Pushbutton [package="[THT]"]
  S3 = Pushbutton [package="[THT]"]
  J1 = Piezo Speaker
  R2 = Resistor [tolerance=±5% resistance=220 package=THT]
  R3 = Resistor [tolerance=±5% resistance=220 package=THT]
  R4 = Photocell (LDR) [package=THT]

nets:
  N1: Part1.A5/SCL, R3.Pin_0, R4.pin_1
  N2: Part1.D9_PWM, J1.pin1
  N3: Part1.D13/SCK, LED1.anode
  N4: Part1.GND, R1.Pin_0, S1.Pin_1, S1.Pin_2, S2.Pin_2, S3.Pin_3, S3.Pin_4, R2.Pin_1, R4.pin_0
  N5: Part1.D2, S2.Pin_4
  N6: Part1.D4, S1.Pin_4
  N7: Part1.D5_PWM, S3.Pin_1, S3.Pin_2
  N8: Part1.5V, R3.Pin_1
  N9: LED1.cathode, R1.Pin_1
  N10: J1.pin2, R2.Pin_0
